# Fritzing sketch Recepteur-Raspi-2_4Ghz (saved by Fritzing 0.9.2b)

parts:
  Raspberry_Pi = Raspberry Pi B rev2
  NRF24L1_Emetteur_2_4Ghz = NRF24L01

nets:
  3V3: Raspberry_Pi.3V3, NRF24L1_Emetteur_2_4Ghz.VCC
  GND: Raspberry_Pi.GND, NRF24L1_Emetteur_2_4Ghz.GND
  N1: Raspberry_Pi.GPIO_10, NRF24L1_Emetteur_2_4Ghz.MOSI
  N2: Raspberry_Pi.GPIO_9, NRF24L1_Emetteur_2_4Ghz.MISO
  N3: Raspberry_Pi.GPIO_25, NRF24L1_Emetteur_2_4Ghz.CE
  N4: Raspberry_Pi.GPIO_11, NRF24L1_Emetteur_2_4Ghz.SCK
  N5: Raspberry_Pi.GPIO_8, NRF24L1_Emetteur_2_4Ghz.CSN

custom parts:
  NRF24L01: NRF24L01 module
