# Fritzing sketch schema_multi_capteur (saved by Fritzing 0.9.2b)

parts:
  Arduino = Arduino Uno (Rev3) - ICSP
  NRF24L1_Emetteur_2_4Ghz = NRF24L01
  DHT22_Humidité/Température = Humidity and Temperature Sensor RHT03
  BMP180_Presion/Température = Barometric Pressure Sensor - BMP085 Breakout
  R1 = Resistor [tolerance=±5% resistance=4.7k package=THT]  # not connected
  R2 = Resistor [tolerance=±5% resistance=4.7k package=THT]  # not connected
  Température_extérieur = DS18B20 1-Wire Temperature Sensor

nets:
  N1: Arduino.A4/SDA, BMP180_Presion/Température.SDA
  N2: Arduino.A5/SCL, BMP180_Presion/Température.SCL
  N3: Arduino.D9_PWM, NRF24L1_Emetteur_2_4Ghz.CE
  N4: Arduino.D10_PWM/SS, NRF24L1_Emetteur_2_4Ghz.CSN
  N5: Arduino.D11_PWM/MOSI, NRF24L1_Emetteur_2_4Ghz.MOSI
  N6: Arduino.D12/MISO, NRF24L1_Emetteur_2_4Ghz.MISO
  N7: Arduino.D13/SCK, NRF24L1_Emetteur_2_4Ghz.SCK
  N8: Arduino.D2, NRF24L1_Emetteur_2_4Ghz.IRQ
  N9: Arduino.D6_PWM, DHT22_Humidité/Température.Data-signal
  N10: Arduino.D7, Température_extérieur.DQ
  3V3: Arduino.3V3, NRF24L1_Emetteur_2_4Ghz.VCC
  5V: Arduino.5V, DHT22_Humidité/Température.Vcc
  GND: Arduino.GND, NRF24L1_Emetteur_2_4Ghz.GND

custom parts:
  NRF24L01: NRF24L01 module
